// Logisim project 3bitcounter.circ as structural Verilog: 1 circuit, main circuit main
module main (
);

  wire and_1_out, and_2_out, clock_1_out, clock_2_out, d_ff_1_q, d_ff_2_q, d_ff_3_q, j_k_ff_1_q, j_k_ff_2_q,
       j_k_ff_3_q, not_1_out, xor_1_out, xor_2_out, xor_3_out;

  Clock clock_1 (.out(clock_1_out));
  D_Flip_Flop d_ff_1 (.clk(clock_1_out), .D(xor_3_out), .Q(d_ff_1_q));  // open: Qn, preset, en, reset
  D_Flip_Flop d_ff_2 (.clk(clock_1_out), .D(xor_2_out), .Q(d_ff_2_q));  // open: Qn, preset, en, reset
  Clock clock_2 (.out(clock_2_out));
  D_Flip_Flop d_ff_3 (.clk(clock_1_out), .D(xor_1_out), .Q(d_ff_3_q));  // open: Qn, preset, en, reset
  xor xor_1 (xor_1_out, d_ff_3_q, 1'b1);
  and and_1 (and_1_out, d_ff_3_q, 1'b1);
  J_K_Flip_Flop j_k_ff_1 (
    .J(j_k_ff_2_q), .clk(clock_2_out), .K(j_k_ff_1_q), .Q(j_k_ff_1_q));  // open: Qn, preset, en, reset
  J_K_Flip_Flop j_k_ff_2 (
    .J(j_k_ff_3_q), .clk(clock_2_out), .K(j_k_ff_2_q), .Q(j_k_ff_2_q));  // open: Qn, preset, en, reset
  not not_1 (not_1_out, j_k_ff_3_q);
  J_K_Flip_Flop j_k_ff_3 (
    .J(not_1_out), .clk(clock_2_out), .K(j_k_ff_3_q), .Q(j_k_ff_3_q));  // open: Qn, preset, en, reset
  xor xor_2 (xor_2_out, d_ff_2_q, and_1_out);
  and and_2 (and_2_out, d_ff_2_q, and_1_out);
  xor xor_3 (xor_3_out, d_ff_1_q, and_2_out);

  // Notes on the sheet:
  //   Q
  //   J     K
  //   0
  //   1
  //   1
  //   0
  //   0
  //   1
  //   0
  //   0
  //   1
  //   1
  //   не изменяется
  //   инверсия по такту
  //   сумматор?
  //   000 001 010 011 100 101 110 111
endmodule
