// Logisim project comparison.circ as structural Verilog: 1 circuit, main circuit main
module main (
);

  wire and_1_out, and_2_out, and_3_out, and_4_out, and_5_out, and_6_out, and_7_out, and_8_out, and_9_out,
       and_10_out, and_11_out, and_12_out, and_13_out, and_14_out, and_15_out, and_16_out, not_1_out,
       not_2_out, not_3_out, not_4_out, not_5_out, not_6_out, not_7_out, not_8_out, not_9_out, not_10_out,
       not_11_out, not_12_out, or_1_out, or_2_out, or_3_out, or_4_out, undriven, undriven_2, undriven_3,
       undriven_4, undriven_5, undriven_6, undriven_7, undriven_8, undriven_9, undriven_10, undriven_11,
       undriven_12, undriven_13, undriven_14, undriven_15, undriven_16, undriven_17, undriven_18,
       undriven_19, undriven_20, undriven_21, undriven_22, undriven_23, undriven_24, undriven_25,
       undriven_26, undriven_27, undriven_28, undriven_29, undriven_30, undriven_31, undriven_32,
       undriven_33, undriven_34, undriven_35, undriven_36, undriven_37, undriven_38, undriven_39,
       undriven_40, undriven_41, undriven_42, undriven_43, undriven_44, xnor_1_out, xnor_2_out, xnor_3_out,
       xnor_4_out, xnor_5_out, xnor_6_out, xnor_7_out, xnor_8_out, xnor_9_out, xnor_10_out;

  xnor xnor_1 (xnor_1_out, undriven, undriven_11);
  xnor xnor_2 (xnor_2_out, undriven_4, undriven_12);
  xnor xnor_3 (xnor_3_out, undriven_13, undriven_14);
  not not_1 (not_1_out, undriven_2);
  not not_2 (not_2_out, undriven_5);
  not not_3 (not_3_out, undriven_7);
  not not_4 (not_4_out, undriven_8);
  not not_5 (not_5_out, undriven_9);
  not not_6 (not_6_out, undriven_10);
  and and_1 (and_1_out, xnor_1_out, xnor_2_out, xnor_3_out);
  and and_2 (and_2_out, not_1_out, undriven_15);
  and and_3 (and_3_out, xnor_1_out, not_2_out, undriven_16);
  and and_4 (and_4_out, xnor_1_out, xnor_2_out, not_3_out, undriven_17);
  and and_5 (and_5_out, undriven_3, not_4_out);
  and and_6 (and_6_out, xnor_1_out, undriven_6, not_5_out);
  and and_7 (and_7_out, xnor_1_out, xnor_2_out, undriven_18, not_6_out);
  or or_1 (or_1_out, and_2_out, and_3_out, and_4_out);
  or or_2 (or_2_out, and_5_out, and_6_out, and_7_out);
  xnor xnor_4 (xnor_4_out, undriven_19, undriven_21);
  xnor xnor_5 (xnor_5_out, undriven_20, undriven_22);
  xnor xnor_6 (xnor_6_out, undriven_23, undriven_24);
  xnor xnor_7 (xnor_7_out, undriven_25, undriven_26);
  and and_8 (and_8_out, xnor_4_out, xnor_6_out);
  and and_9 (and_9_out, xnor_5_out, xnor_7_out);
  not not_7 (not_7_out, undriven_27);
  not not_8 (not_8_out, undriven_29);
  not not_9 (not_9_out, undriven_31);
  and and_10 (and_10_out, not_7_out, undriven_28);
  and and_11 (and_11_out, not_8_out, xnor_4_out, xnor_4_out, undriven_30);
  and and_12 (and_12_out, not_9_out, and_8_out, undriven_32);
  not not_10 (not_10_out, undriven_34);
  not not_11 (not_11_out, undriven_36);
  not not_12 (not_12_out, undriven_38);
  xnor xnor_8 (xnor_8_out, undriven_39, undriven_40);
  xnor xnor_9 (xnor_9_out, undriven_41, undriven_42);
  xnor xnor_10 (xnor_10_out, undriven_43, undriven_44);
  and and_13 (and_13_out, undriven_33, not_10_out);
  and and_14 (and_14_out, undriven_35, xnor_5_out, xnor_5_out, not_11_out);
  and and_15 (and_15_out, undriven_37, and_9_out, not_12_out);
  or or_3 (or_3_out, and_10_out, and_11_out, and_12_out);
  or or_4 (or_4_out, and_13_out, and_14_out, and_15_out);
  and and_16 (and_16_out, xnor_8_out, xnor_9_out, xnor_10_out);

  // Notes on the sheet:
  //   A
  //   B
  //   A2
  //   A1
  //   A0
  //   B2
  //   B1
  //   B0
  //   A2 ⊙ B2
  //   A1 ⊙ B1
  //   A0 ⊙ B0
  //   ¬A2 ∧ B2
  //   ¬A1 ∧ B1
  //   ¬A0 ∧ B0
  //   A2 ∧ ¬B2
  //   A1 ∧ ¬B1
  //   A0 ∧ ¬B0
  //   EQ
  //   LT
  //   GT
  //   A2
  //   B2
  //   A1
  //   B1
  //   A0
  //   B0
  //   A2
  //   B2
  //   A1
  //   B1
  //   A0
  //   B0
  //   A2
  //   B2
  //   A1
  //   B1
  //   A0
  //   B0
  //   LT
  //   GT
  //   EQ
endmodule
