// Logisim project scheme.circ as structural Verilog: 1 circuit, main circuit main
module main (
  input  [2:0] in_1,
  input  [2:0] in_2,
  input  [1:0] R1R0,
  input  L,
  input  M
);

  wire _0_out, _1_out, _2_out, _3_out, and_1_out, and_2_out, and_3_out, and_4_out, and_5_out, and_6_out,
       and_7_out, and_8_out, and_9_out, and_10_out, and_11_out, AUTO_out, B_out, clock_1_out, d_ff_1_q,
       MANUAL_out, nor_1_out, not_1_out, not_2_out, not_3_out, not_4_out, OFF_out, ON_out, or_1_out,
       or_2_out, or_3_out, or_4_out, or_5_out, or_6_out, or_7_out, or_8_out, or_9_out, or_10_out, or_11_out,
       or_12_out, or_13_out, or_14_out, or_15_out, or_16_out, or_17_out, xor_1_out, xor_2_out, xor_3_out,
       xor_4_out, xor_5_out, xor_6_out, xor_7_out;

  // Probe on or_1_out
  // Probe on xor_1_out
  or or_1 (or_1_out, or_8_out, or_9_out);
  _7_Segment_Display u_7_segment_display_1 (
    .g(or_2_out), .f(_0_out), .a(or_3_out), .b(or_4_out), .e(or_7_out), .d(or_6_out), .c(or_5_out),
    .dp(or_11_out));
  xor xor_1 (xor_1_out, xor_2_out, or_10_out);
  or or_2 (or_2_out, _3_out, _2_out);
  or or_3 (or_3_out, _0_out, _3_out, _2_out);
  or or_4 (or_4_out, _1_out, _2_out, _3_out, _0_out);
  or or_5 (or_5_out, _1_out, _0_out, _3_out);
  or or_6 (or_6_out, _2_out, _3_out, _0_out);
  or or_7 (or_7_out, _2_out, _0_out);
  or or_8 (or_8_out, and_1_out, and_2_out);
  or or_9 (or_9_out, and_2_out, and_3_out);
  xor xor_2 (xor_2_out, in_1[2], in_2[2]);
  and and_1 (and_1_out, in_1[2], in_2[2]);
  and and_2 (and_2_out, in_1[2], or_10_out);
  and and_3 (and_3_out, in_2[2], or_10_out);
  and _1 (_1_out, R1R0[0], not_1_out);
  and _3 (_3_out, R1R0[0], R1R0[1]);
  and _2 (_2_out, not_2_out, R1R0[1]);
  nor _0 (_0_out, R1R0[0], R1R0[1]);
  not not_1 (not_1_out, R1R0[1]);
  not not_2 (not_2_out, R1R0[0]);
  // Probe on xor_3_out
  or or_10 (or_10_out, or_12_out, or_13_out);
  or or_11 (or_11_out, OFF_out, ON_out, AUTO_out, d_ff_1_q);
  xor xor_3 (xor_3_out, xor_4_out, or_15_out);
  or or_12 (or_12_out, and_4_out, and_5_out);
  or or_13 (or_13_out, and_5_out, and_6_out);
  xor xor_4 (xor_4_out, in_2[1], in_1[1]);
  and and_4 (and_4_out, in_2[1], or_15_out);
  and and_5 (and_5_out, in_2[1], or_15_out);
  and and_6 (and_6_out, in_1[1], or_15_out);
  Clock clock_1 (.out(clock_1_out));
  xor xor_5 (xor_5_out, MANUAL_out, d_ff_1_q);
  D_Flip_Flop d_ff_1 (.clk(clock_1_out), .D(xor_5_out), .Q(d_ff_1_q), .reset(or_14_out));  // open: Qn, preset, en
  or or_14 (or_14_out, AUTO_out, ON_out, OFF_out);
  // Probe on xor_6_out
  or or_15 (or_15_out, or_16_out, or_17_out);
  and ON (ON_out, not_3_out, R1R0[1]);
  and AUTO (AUTO_out, nor_1_out, and_11_out);
  and MANUAL (MANUAL_out, and_7_out, B_out);
  buf xor_6 (xor_6_out, xor_7_out);  // XOR_Gate
  or or_16 (or_16_out, and_8_out, and_9_out);
  or or_17 (or_17_out, and_9_out, and_10_out);
  and OFF (OFF_out, R1R0[0], R1R0[1]);
  not not_3 (not_3_out, R1R0[0]);
  nor nor_1 (nor_1_out, R1R0[0], R1R0[1]);
  and and_7 (and_7_out, R1R0[0], not_4_out);
  not not_4 (not_4_out, R1R0[1]);
  xor xor_7 (xor_7_out, in_2[0], in_1[0]);
  and and_8 (and_8_out, in_2[0], in_1[0]);
  and and_9 (and_9_out, in_2[0], in_1[0]);
  and and_10 (and_10_out, in_2[0], in_1[0]);
  and and_11 (and_11_out, L, M);
  Button B (.out(B_out));
endmodule
