// Logisim project d-trigger.circ as structural Verilog: 1 circuit, main circuit main
module main (
  output out_1
);

  wire and_1_out, and_2_out, clock_1_out, not_1_out, S_out;

  Clock clock_1 (.out(clock_1_out));
  and and_1 (and_1_out, clock_1_out, 1'b1);
  not not_1 (not_1_out, 1'b1);
  and and_2 (and_2_out, not_1_out, clock_1_out);
  nor R (out_1, S_out, and_2_out);
  nor S (S_out, out_1, and_1_out);
endmodule
