// Logisim project doors-fsm.circ as structural Verilog: 1 circuit, main circuit main
module main (
  input  in_1,
  input  in_2
);

  wire and_1_out, and_2_out, and_3_out, and_4_out, and_5_out, clock_1_out, d_ff_1_q, j_k_ff_1_q, j_k_ff_1_qn,
       nor_1_out, OPEN_D1_2_out, OPEN_D1_q, OPEN_D1_qn, OPEN_D2_2_out, OPEN_D2_q, OPEN_D2_qn, or_1_out,
       WAIT_D1_q, WAIT_D2_q, WAIT_IN_q, WAIT_OUT_q;

  Clock clock_1 (.out(clock_1_out));
  nor nor_1 (nor_1_out, or_1_out, in_2, in_1);
  and and_1 (and_1_out, in_2, in_1);
  // Probe on and_1_out
  D_Flip_Flop d_ff_1 (.clk(clock_1_out), .D(nor_1_out), .Q(d_ff_1_q));  // open: Qn, preset, en, reset
  // Probe on d_ff_1_q
  and and_2 (and_2_out, d_ff_1_q, ~and_1_out, in_1);  // AND_Gate
  and and_3 (and_3_out, d_ff_1_q, ~and_1_out, in_2);  // AND_Gate
  J_K_Flip_Flop j_k_ff_1 (
    .J(and_2_out), .clk(clock_1_out), .K(and_3_out), .Q(j_k_ff_1_q), .Qn(j_k_ff_1_qn));  // open: preset, en, reset
  and and_4 (and_4_out, in_1, j_k_ff_1_q);
  and and_5 (and_5_out, j_k_ff_1_qn, in_2);
  D_Flip_Flop OPEN_D1 (.clk(clock_1_out), .D(and_4_out), .Q(OPEN_D1_q), .Qn(OPEN_D1_qn));  // open: preset, en, reset
  D_Flip_Flop OPEN_D2 (.clk(clock_1_out), .D(and_5_out), .Q(OPEN_D2_q), .Qn(OPEN_D2_qn));  // open: preset, en, reset
  D_Flip_Flop WAIT_D1 (.clk(clock_1_out), .D(OPEN_D1_q), .Q(WAIT_D1_q));  // open: Qn, preset, en, reset
  D_Flip_Flop WAIT_D2 (.clk(clock_1_out), .D(OPEN_D2_q), .Q(WAIT_D2_q));  // open: Qn, preset, en, reset
  and OPEN_D2_2 (OPEN_D2_2_out, WAIT_D1_q, OPEN_D1_qn);
  and OPEN_D1_2 (OPEN_D1_2_out, WAIT_D2_q, OPEN_D2_qn);
  or or_1 (or_1_out, WAIT_IN_q, WAIT_OUT_q);
  T_Flip_Flop WAIT_IN (.clk(clock_1_out), .T(OPEN_D2_2_out), .Q(WAIT_IN_q), .reset(in_2));  // open: Qn, preset, en
  T_Flip_Flop WAIT_OUT (.clk(clock_1_out), .T(OPEN_D1_2_out), .Q(WAIT_OUT_q), .reset(in_1));  // open: Qn, preset, en
endmodule
