// Logisim project jk-trigger.circ as structural Verilog: 1 circuit, main circuit main
module main (
  input  [1:0] in_1
);

  wire and_1_out, and_2_out, and_3_out, and_4_out, and_5_out, and_6_out, and_7_out, and_8_out, clock_1_out,
       nor_1_out, nor_2_out, nor_3_out, nor_4_out, not_1_out, not_2_out, not_3_out, not_4_out, not_5_out,
       not_6_out, or_1_out, or_2_out, R_out, S_out, T_out, xor_1_out;

  not not_1 (not_1_out, in_1[1]);
  not not_2 (not_2_out, in_1[0]);
  and T (T_out, in_1[0], in_1[1]);
  and R (R_out, not_1_out, in_1[0]);
  not not_3 (not_3_out, nor_3_out);
  and S (S_out, in_1[1], not_2_out);
  not not_4 (not_4_out, xor_1_out);
  xor xor_1 (xor_1_out, nor_3_out, T_out);
  and and_1 (and_1_out, R_out, nor_3_out);
  and and_2 (and_2_out, not_3_out, S_out);
  and and_3 (and_3_out, not_4_out, T_out);
  and and_4 (and_4_out, T_out, xor_1_out);
  or or_1 (or_1_out, and_3_out, and_1_out);
  or or_2 (or_2_out, and_4_out, and_2_out);
  Clock clock_1 (.out(clock_1_out));
  // Probe on nor_3_out
  not not_5 (not_5_out, clock_1_out);
  and and_5 (and_5_out, not_5_out, or_1_out);
  and and_6 (and_6_out, or_2_out, not_5_out);
  and and_7 (and_7_out, clock_1_out, not_6_out);
  not not_6 (not_6_out, nor_1_out);
  and and_8 (and_8_out, nor_1_out, clock_1_out);
  nor nor_1 (nor_1_out, nor_2_out, and_5_out);
  nor nor_2 (nor_2_out, nor_1_out, and_6_out);
  nor nor_3 (nor_3_out, nor_4_out, and_7_out);
  nor nor_4 (nor_4_out, nor_3_out, and_8_out);
endmodule
