// Logisim project MOSFET_Elements.circ as structural Verilog: 1 circuit, main circuit main
module main (
  input  in_1,
  input  in_2,
  input  in_3,
  input  in_4,
  input  in_5,
  input  in_6,
  input  in_7,
  input  in_8,
  input  in_9,
  input  in_10
);

  wire transistor_1_out, transistor_2_out, transistor_3_out, transistor_6_out, transistor_8_out,
       transistor_10_out, transistor_13_out, transistor_15_out, transistor_16_out, transistor_17_out,
       transistor_18_out, transistor_19_out, transistor_23_out, transistor_26_out, transistor_27_out,
       transistor_28_out, transistor_33_out, transistor_34_out, transistor_36_out, transistor_38_out,
       transistor_41_out, transistor_42_out, transistor_43_out, transistor_46_out, transistor_47_out,
       transistor_49_out, transistor_52_out;

  Transistor #(.\type ("n")) transistor_1 (.in(in_8), .out(transistor_1_out), .gate(in_8));
  Transistor transistor_2 (.in(1'b0), .out(transistor_2_out), .gate(in_8));
  // NOT_Gate not_1 is placed but not wired
  Transistor #(.\type ("n")) transistor_3 (.in(1'b0), .out(transistor_3_out), .gate(in_1));
  Transistor transistor_4 (.in(1'b1), .out(transistor_3_out), .gate(in_1));
  // OR_Gate or_1 is placed but not wired
  Transistor #(.\type ("n")) transistor_5 (.in(in_9), .out(transistor_1_out), .gate(in_9));
  Transistor transistor_6 (.in(transistor_2_out), .out(transistor_6_out), .gate(in_9));
  // Probe on transistor_3_out
  Transistor #(.\type ("n")) transistor_7 (.in(in_10), .out(transistor_1_out), .gate(in_10));
  Transistor transistor_8 (.in(1'b0), .out(transistor_8_out), .gate(in_2));
  // Probe on transistor_1_out
  Transistor transistor_9 (.in(transistor_6_out), .out(transistor_1_out), .gate(in_10));
  Transistor #(.\type ("n")) transistor_10 (.in(in_2), .out(transistor_10_out), .gate(in_2));
  Transistor transistor_11 (.in(1'b0), .out(transistor_8_out), .gate(in_3));
  // AND_Gate and_1 is placed but not wired
  Transistor #(.\type ("n")) transistor_12 (.in(transistor_13_out), .out(transistor_8_out), .gate(in_4));
  Transistor #(.\type ("n")) transistor_13 (.in(transistor_10_out), .out(transistor_13_out), .gate(in_3));
  Transistor transistor_14 (.in(1'b0), .out(transistor_8_out), .gate(in_4));
  Transistor transistor_15 (.in(1'b0), .out(transistor_15_out), .gate(in_5));
  Transistor #(.\type ("n")) transistor_16 (.in(in_5), .out(transistor_16_out), .gate(in_5));
  Transistor transistor_17 (.in(1'b0), .out(transistor_17_out), .gate(in_5));
  // Probe on transistor_8_out
  Transistor #(.\type ("n")) transistor_18 (.in(in_5), .out(transistor_18_out), .gate(in_5));
  Transistor #(.\type ("n")) transistor_19 (.in(in_5), .out(transistor_19_out), .gate(in_5));
  Transistor transistor_20 (.in(1'b0), .out(transistor_15_out), .gate(in_6));
  Transistor #(.\type ("n")) transistor_21 (.in(transistor_16_out), .out(transistor_17_out), .gate(in_7));
  Transistor transistor_22 (.in(1'b0), .out(transistor_17_out), .gate(in_7));
  Transistor transistor_23 (.in(1'b0), .out(transistor_23_out), .gate(in_5));
  Transistor #(.\type ("n")) transistor_24 (.in(transistor_19_out), .out(transistor_15_out), .gate(in_6));
  Transistor #(.\type ("n")) transistor_25 (.in(in_6), .out(transistor_18_out), .gate(in_6));
  Transistor transistor_26 (.in(transistor_23_out), .out(transistor_26_out), .gate(in_6));
  Transistor #(.\type ("n")) transistor_27 (.in(in_6), .out(transistor_27_out), .gate(in_6));
  Transistor transistor_28 (.in(1'b0), .out(transistor_28_out), .gate(in_6));
  Transistor #(.\type ("n")) transistor_29 (.in(in_7), .out(transistor_18_out), .gate(in_7));
  Transistor transistor_30 (.in(transistor_26_out), .out(transistor_18_out), .gate(in_7));
  Transistor #(.\type ("n")) transistor_31 (.in(transistor_27_out), .out(transistor_28_out), .gate(in_7));
  Transistor transistor_32 (.in(1'b0), .out(transistor_28_out), .gate(in_7));
  Transistor #(.\type ("n")) transistor_33 (.in(transistor_28_out), .out(transistor_33_out), .gate(transistor_28_out));
  // XOR_Gate xor_1 is placed but not wired
  Transistor #(.\type ("n")) transistor_34 (.in(1'b0), .out(transistor_34_out), .gate(transistor_33_out));
  Transistor #(.\type ("n")) transistor_35 (.in(transistor_17_out), .out(transistor_33_out), .gate(transistor_17_out));
  Transistor transistor_36 (.in(1'b0), .out(transistor_36_out), .gate(transistor_28_out));
  Transistor transistor_37 (.in(1'b1), .out(transistor_34_out), .gate(transistor_33_out));
  Transistor transistor_38 (.in(transistor_36_out), .out(transistor_38_out), .gate(transistor_17_out));
  Transistor #(.\type ("n")) transistor_39 (.in(transistor_15_out), .out(transistor_33_out), .gate(transistor_15_out));
  Transistor transistor_40 (.in(transistor_38_out), .out(transistor_33_out), .gate(transistor_15_out));
  Transistor #(.\type ("n")) transistor_41 (.in(transistor_43_out), .out(transistor_41_out), .gate(transistor_43_out));
  Transistor transistor_42 (.in(1'b0), .out(transistor_42_out), .gate(transistor_43_out));
  Transistor transistor_43 (.in(1'b0), .out(transistor_43_out), .gate(transistor_28_out));
  Transistor #(.\type ("n")) transistor_44 (.in(transistor_34_out), .out(transistor_41_out), .gate(transistor_34_out));
  Transistor transistor_45 (.in(transistor_42_out), .out(transistor_41_out), .gate(transistor_34_out));
  Transistor #(.\type ("n")) transistor_46 (.in(transistor_28_out), .out(transistor_46_out), .gate(transistor_28_out));
  Transistor #(.\type ("n")) transistor_47 (.in(transistor_46_out), .out(transistor_47_out), .gate(transistor_17_out));
  Transistor transistor_48 (.in(1'b0), .out(transistor_43_out), .gate(transistor_17_out));
  Transistor transistor_49 (.in(1'b0), .out(transistor_49_out), .gate(transistor_41_out));
  Transistor #(.\type ("n")) transistor_50 (.in(transistor_47_out), .out(transistor_43_out), .gate(transistor_15_out));
  Transistor transistor_51 (.in(1'b0), .out(transistor_43_out), .gate(transistor_15_out));
  Transistor #(.\type ("n")) transistor_52 (.in(transistor_18_out), .out(transistor_52_out), .gate(transistor_41_out));
  Transistor transistor_53 (.in(1'b0), .out(transistor_49_out), .gate(transistor_18_out));
  // Probe on transistor_49_out
  Transistor #(.\type ("n")) transistor_54 (.in(transistor_52_out), .out(transistor_49_out), .gate(transistor_18_out));
endmodule
