// Logisim project t-trigger.circ as structural Verilog: 1 circuit, main circuit main
module main (
);

  wire and_1_out, and_2_out, and_3_out, and_4_out, and_5_out, and_6_out, button_1_out, clock_1_out,
       clock_2_out, clock_3_out, d_ff_1_q, not_1_out, not_2_out, not_3_out, not_4_out, R_2_out, R_3_out,
       R_out, S_2_out, S_3_out, S_out, T_2_out, T_out, xor_1_out, xor_2_out;

  Clock clock_1 (.out(clock_1_out));
  not not_1 (not_1_out, clock_1_out);
  LED led_1 (.in(R_2_out));
  Button T (.out(T_out));
  xor xor_1 (xor_1_out, T_out, R_2_out);
  Clock clock_2 (.out(clock_2_out));
  Button T_2 (.out(T_2_out));
  not not_2 (not_2_out, xor_1_out);
  not not_3 (not_3_out, R_out);
  and and_1 (and_1_out, not_1_out, not_2_out);
  and and_2 (and_2_out, xor_1_out, not_1_out);
  and and_3 (and_3_out, clock_1_out, not_3_out);
  and and_4 (and_4_out, R_out, clock_1_out);
  not not_4 (not_4_out, R_3_out);
  and and_5 (and_5_out, clock_2_out, T_2_out, not_4_out);
  and and_6 (and_6_out, R_3_out, T_2_out, clock_2_out);
  nor R (R_out, S_out, and_1_out);
  nor S (S_out, R_out, and_2_out);
  nor R_2 (R_2_out, S_2_out, and_3_out);
  nor S_2 (S_2_out, R_2_out, and_4_out);
  nor R_3 (R_3_out, S_3_out, and_5_out);
  nor S_3 (S_3_out, R_3_out, and_6_out);
  Button button_1 (.out(button_1_out));
  xor xor_2 (xor_2_out, d_ff_1_q, button_1_out);
  Clock clock_3 (.out(clock_3_out));
  D_Flip_Flop d_ff_1 (.clk(clock_3_out), .D(xor_2_out), .Q(d_ff_1_q));  // open: Qn, preset, en, reset
endmodule
